# Fritzing sketch diagrama proyecto policiaco (saved by Fritzing 0.9.10b)
breadboards: 2

parts:
  U1 = RFID RC522 SIP - 8 pins [chip_label="RFID RC522" package="SIP (Single Inline) [THT]"]
  M1 = DOIT Esp32 DevKit v1 (30 pins long, 11 pins width) [part_number=ESP32S-PIN30]
  M2 = DOIT Esp32 DevKit v1 (30 pins long, 11 pins width) [part_number=ESP32S-PIN30]
  U2 = RFID RC522 SIP - 8 pins [chip_label="RFID RC522" package="SIP (Single Inline) [THT]"]
  J1 = Basic Servo
  LED1 = LED - 3mm [color="Red (633nm)" current=0.030 package="3 mm [THT]"]
  LED2 = LED - 3mm [color="Blue (430nm)" current=0.030 package="3 mm [THT]"]  # not connected
  LED3 = LED - 3mm [color="Red (633nm)" current=0.030 package="3 mm [THT]"]
  LED4 = LED - 3mm [color="Blue (430nm)" current=0.030 package="3 mm [THT]"]

nets:
  N1: U1.IRQ, M1.D5
  N2: U1.NSS, M1.D18
  N3: U1.SCK, M1.D23
  N4: U1.MOSI, M1.D19
  GND: U1.GND, M1.GND, LED1.cathode
  N5: U1.RST, M1.D22
  VCC: U1.VCC, M1.3V3
  N6: M1.D33, LED1.anode
  VCC_2: M2.3V3, U2.VCC, J1.vcc
  GND_2: M2.GND, U2.GND, J1.gnd, LED3.cathode, LED4.cathode
  N7: M2.D5, U2.IRQ
  N8: M2.D18, U2.NSS
  N9: M2.D19, U2.MOSI
  N10: M2.D22, U2.RST
  N11: M2.D23, U2.SCK
  N12: M2.D32, LED4.anode
  N13: M2.D33, LED3.anode
  N14: M2.D13, J1.pulse

notes:
  Los pines de entrada de izquierda a derecha son :
  SDA, SCK MOSI, MISO, IRQ, GND, RST, 3.3V

custom parts:
  RFID RC522 SIP - 8 pins: A SIP stand-in part for RFID RC522 . With 8 pins on a 300 mil single inline package (SIP) footprint.
  DOIT Esp32 DevKit v1 (30 pins long, 11 pins width): The DOIT Esp32 DevKit v1 is one of the development board created by DOIT to evaluate the ESP-WROOM-32 module. It is based on the ESP32 microcontroller that boasts Wifi, Bluetooth, Ethernet and Low Power support all in a single chip. (vanepp) made breadboard work, adjusted pin numbering and labels and reduced size of schematic and cleaned up pcb. This chip is 30pins long (2 x15) and 11 pins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
